# Fritzing sketch radlicht (saved by Fritzing 0.8.5b)
circuit board: 15.78cm x 8.24311cm
breadboards: 1

parts:
  U1 = 74HC595 [package="DIP16 [THT]"]
  IC1 = ULN2803A [package=THT]
  LED1 = LED - 5mm [color="Red (633nm)" package="5 mm [THT]"]
  LED2 = LED - 5mm [color="Red (633nm)" package="5 mm [THT]"]
  LED3 = LED - 5mm [color="Red (633nm)" package="5 mm [THT]"]
  LED4 = LED - 5mm [color="Red (633nm)" package="5 mm [THT]"]
  R1 = Resistor [tolerance=±5% resistance=220 package=THT]
  R2 = Resistor [tolerance=±5% resistance=220 package=THT]
  R4 = Resistor [tolerance=±5% resistance=220 package=THT]
  R5 = Resistor [tolerance=±5% resistance=220 package=THT]
  R6 = Resistor [tolerance=±5% resistance=220 package=THT]
  R7 = Resistor [tolerance=±5% resistance=220 package=THT]
  R8 = Resistor [tolerance=±5% resistance=220 package=THT]
  LED5 = LED - 5mm [color="Red (633nm)" package="5 mm [THT]"]
  LED6 = LED - 5mm [color="Red (633nm)" package="5 mm [THT]"]
  LED7 = LED - 5mm [color="Red (633nm)" package="5 mm [THT]"]
  LED8 = LED - 5mm [color="Red (633nm)" package="5 mm [THT]"]
  R3 = Resistor [tolerance=±5% resistance=220 package=THT]
  Bauteil1 = Arduino Pro Mini v13
  S1 = Reed switch [package=THT]
  R9 = Resistor [tolerance=±5% resistance=220 package=THT]
  VCC1 = Battery

nets:
  N1: U1.Q1, IC1.In_7
  N2: U1.Q2, IC1.In_6
  N3: U1.Q3, IC1.In_5
  N4: U1.Q4, IC1.In_4
  N5: U1.Q5, IC1.In_3
  N6: U1.Q6, IC1.In_2
  N7: U1.Q7, IC1.In_1
  GND: U1.GND, U1.OE, IC1.0V, Bauteil1.GND, R9.Pin_1, VCC1.-
  VCC: U1.MR, U1.VCC, LED1.anode, LED2.anode, LED3.anode, LED4.anode, LED5.anode, LED6.anode, LED7.anode, LED8.anode, Bauteil1.VCC, S1.pin_1, VCC1.+
  N8: U1.SH_CP, Bauteil1.D6_PWM
  N9: U1.ST_CP, Bauteil1.D5_PWM
  N10: U1.DS, Bauteil1.D4
  N11: U1.Q0, IC1.In_8
  N12: IC1.Out_8, R8.Pin_0
  N13: IC1.Out_7, R7.Pin_0
  N14: IC1.Out_6, R6.Pin_0
  N15: IC1.Out_5, R5.Pin_0
  N16: IC1.Out_4, R3.Pin_0
  N17: IC1.Out_3, R2.Pin_0
  N18: IC1.Out_2, R1.Pin_0
  N19: IC1.Out_1, R4.Pin_0
  N20: LED1.cathode, R4.Pin_1
  N21: LED2.cathode, R1.Pin_1
  N22: LED3.cathode, R2.Pin_1
  N23: LED4.cathode, R3.Pin_1
  N24: R5.Pin_1, LED5.cathode
  N25: R6.Pin_1, LED6.cathode
  N26: R7.Pin_1, LED7.cathode
  N27: R8.Pin_1, LED8.cathode
  N28: Bauteil1.D2, S1.pin_2, R9.Pin_0
